// Logisim project 1001自动检测moore.circ as structural Verilog: 1 circuit, main circuit main
module main (
  input  \输入X ,
  output Z
);

  wire and_1_out, and_2_out, and_3_out, and_4_out, and_5_out, clock_1_out, D1_q, D1_qn, D2_q, D2_qn, D3_q,
       D3_qn, not_1_out, not_2_out, or_1_out, or_2_out, or_3_out, or_4_out;

  Clock #(.highDuration(1), .lowDuration(1)) clock_1 (.out(clock_1_out));
  and and_1 (and_1_out, \输入X , D3_qn, D2_qn, D1_q);
  D_Flip_Flop #(.trigger("rising"), .Pre_Clr_Positions("ABOVE_BELOW"), .NegatePresetClear("false"), .enable("false"), .NewFFLayout("true")) D3 (
    .clk(clock_1_out), .D(and_1_out), .Q(D3_q), .Qn(D3_qn));  // open: preset, reset
  D_Flip_Flop #(.trigger("rising"), .Pre_Clr_Positions("ABOVE_BELOW"), .NegatePresetClear("false"), .enable("false"), .NewFFLayout("true")) D2 (
    .clk(clock_1_out), .D(and_2_out), .Q(D2_q), .Qn(D2_qn));  // open: preset, reset
  D_Flip_Flop #(.trigger("rising"), .Pre_Clr_Positions("ABOVE_BELOW"), .NegatePresetClear("false"), .enable("false"), .NewFFLayout("true")) D1 (
    .clk(clock_1_out), .D(or_4_out), .Q(D1_q), .Qn(D1_qn));  // open: preset, reset
  or or_1 (or_1_out, \输入X , D3_q, D2_q, D1_q);
  or or_2 (or_2_out, \输入X , D3_q, D2_qn, D1_qn);
  or or_3 (or_3_out, \输入X , D3_q, D2_q, D1_qn);
  not not_1 (not_1_out, \输入X );
  not not_2 (not_2_out, \输入X );
  and and_2 (and_2_out, or_1_out, or_2_out, or_3_out);
  and and_3 (and_3_out, not_1_out, D3_qn, D2_q);
  and and_4 (and_4_out, not_2_out, D3_q, D2_q, D1_q);
  and and_5 (and_5_out, \输入X , D3_qn, D2_qn, D1_q);
  or or_4 (or_4_out, and_3_out, and_4_out, and_5_out);
  and and_6 (Z, D3_q, D2_q, D1_q);
endmodule
